// Logisim project jk_trig.circ as structural Verilog: 1 circuit, main circuit main
module main (
  input  C,
  input  J,
  input  K,
  output Q,
  output nQ
);

  wire nand_3_out, nand_4_out;

  nand nand_1 (Q, nand_3_out, nQ);
  nand nand_2 (nQ, Q, nand_4_out, C);
  nand nand_3 (nand_3_out, Q, J);
  nand nand_4 (nand_4_out, nQ, K);
endmodule
